# Fritzing sketch obs2_dht11_bmp280_ds18B20 (saved by Fritzing 0.9.3b)
breadboards: 1

parts:
  WeMos_D1_Mini1 = WeMos D1 Mini  # not connected
  DHT1 = DHT11 Humitidy and Temperature Sensor (3 pins)
  M1 = BME280
  R1 = Resistor [tolerance=±5% resistance=4.7k package=THT]
  DS2 = DS18B20 1-Wire Temperature Sensor Probe Cable

nets:
  GND: DHT1.GND, M1.GND, DS2.GND
  VIN: M1.VIN, R1.Pin_0, DS2.VDD
  N1: R1.Pin_1, DS2.DQ

custom parts:
  DHT11 Humitidy and Temperature Sensor (3 pins): DHT11 Humidity and Temperature Sensor (3 pins) from the design created by John De Cristofaro for Adafruit Industries.
  BME280: Temperature Humidity Barometric presure Sensor
